// Logisim project q1_moore.circ as structural Verilog: 1 circuit, main circuit main
module main (
  input  X,
  input  RST,
  output Y
);

  wire and_1_out, CLK_out, Q0_q, Q0_qn, Q1_q, Q1_qn;

  Clock CLK (.out(CLK_out));
  and and_1 (and_1_out, X, Q1_qn, Q0_qn);
  D_Flip_Flop Q1 (.D(Q0_q), .clk(CLK_out), .Q(Q1_q), .Qn(Q1_qn), .reset(RST));  // open: preset
  D_Flip_Flop Q0 (.D(and_1_out), .clk(CLK_out), .Q(Q0_q), .Qn(Q0_qn), .reset(RST));  // open: preset
  or or_1 (Y, Q1_q, Q0_q);
endmodule
