// Logisim project q3_mealy.circ as structural Verilog: 4 circuits, main circuit main
module main (
  input  W,
  input  RST,
  input  [7:0] VALUE,
  input  [1:0] SEL_REG
);

  wire CLK, DONE, LOAD, not_1_out, not_2_out, OP_REG_q, R1_in, R1_out, R2_in, R2_out, R3_in, R3_out, XCHG;
  wire [7:0] DATAOUT;

  Clock u_CLK (.out(CLK));
  not not_1 (not_1_out, XCHG);
  not not_2 (not_2_out, W);
  Decoder #(.disabled("Z"), .select(2)) decoder_1 (
    .out1(R1_in), .out2(R2_in), .out3(R3_in), .sel(SEL_REG), .en(LOAD));  // open: out0
  and and_1 (LOAD, not_1_out, not_2_out);
  control_unit control_unit_1 (
    .W(W), .CLK(CLK), .RST(RST), .Done(DONE), .R3_in(R3_in), .R2_in(R2_in), .R1_in(R1_in), .R3_out(R3_out),
    .R2_out(R2_out), .R1_out(R1_out));
  J_K_Flip_Flop OP_REG (.J(W), .K(DONE), .clk(CLK), .Q(OP_REG_q), .reset(RST));  // open: Qn, preset
  or or_1 (XCHG, W, OP_REG_q);
  register_file register_file_1 (
    .XCHG(XCHG), .LOAD(LOAD), .DATAIN(VALUE), .R3_WR_EN(R3_in), .R3_RD_EN(R3_out), .R2_WR_EN(R2_in),
    .R2_RD_EN(R2_out), .R1_WR_EN(R1_in), .R1_RD_EN(R1_out), .RST(RST), .CLK(CLK), .DATAOUT(DATAOUT));

  // Other names for the same wires on the sheet: DATAIN[7:0] = VALUE
endmodule

module control_unit (
  input  W,
  input  CLK,
  input  RST,
  output Done,
  output R3_in,
  output R2_in,
  output R1_in,
  output R3_out,
  output R2_out,
  output R1_out
);

  wire R0_qn, R1_qn;

  and and_1 (R2_out, R0_qn, R1_qn, W);
  D_Flip_Flop R1 (.D(R1_out), .clk(CLK), .Q(Done), .Qn(R1_qn), .reset(RST));  // open: preset
  D_Flip_Flop R0 (.D(R2_out), .clk(CLK), .Q(R1_out), .Qn(R0_qn), .reset(RST));  // open: preset

  assign R1_in = Done;
  assign R2_in = R1_out;
  assign R3_in = R2_out;
  assign R3_out = Done;
endmodule

module register_file (
  input  XCHG,
  input  LOAD,
  input  [7:0] DATAIN,
  input  R3_WR_EN,
  input  R3_RD_EN,
  input  R2_WR_EN,
  input  R2_RD_EN,
  input  R1_WR_EN,
  input  R1_RD_EN,
  input  RST,
  input  CLK,
  output [7:0] DATAOUT
);

  wire [7:0] controlled_buffer_1_out, R1_q, R2_q, R3_q;

  assign controlled_buffer_1_out = LOAD ? DATAIN : 8'bz;  // Controlled_Buffer controlled_buffer_1
  Register R3 (.D(controlled_buffer_1_out), .en(R3_WR_EN), .clk(CLK), .Q(R3_q), .clr(RST));
  Register R2 (.D(controlled_buffer_1_out), .en(R2_WR_EN), .clk(CLK), .Q(R2_q), .clr(RST));
  Register R1 (.D(controlled_buffer_1_out), .en(R1_WR_EN), .clk(CLK), .Q(R1_q), .clr(RST));
  assign controlled_buffer_1_out = XCHG ? DATAOUT : 8'bz;  // Controlled_Buffer controlled_buffer_2
  assign DATAOUT = R3_RD_EN ? R3_q : 8'bz;  // Controlled_Buffer controlled_buffer_3
  assign DATAOUT = R2_RD_EN ? R2_q : 8'bz;  // Controlled_Buffer controlled_buffer_4
  assign DATAOUT = R1_RD_EN ? R1_q : 8'bz;  // Controlled_Buffer controlled_buffer_5
endmodule

module test (
  output Y1,
  output Y0,
  output Done,
  output R3_in,
  output R2_in,
  output R1_in,
  output R3_out,
  output R2_out,
  output R1_out,
  output Reset
);

  wire CLK_out, R0_qn, R1_qn, RST_out, W_out;

  Clock #(.highDuration(2), .lowDuration(2), .phaseOffset(2)) W (.out(W_out));
  Clock CLK (.out(CLK_out));
  Clock #(.highDuration(100)) RST (.out(RST_out));
  not not_1 (Reset, RST_out);
  and and_1 (R2_out, R0_qn, R1_qn, W_out);
  D_Flip_Flop R1 (.D(R1_out), .clk(CLK_out), .Q(Done), .Qn(R1_qn), .reset(Reset));  // open: preset
  D_Flip_Flop R0 (.D(R2_out), .clk(CLK_out), .Q(R1_out), .Qn(R0_qn), .reset(Reset));  // open: preset

  assign R1_in = Done;
  assign R2_in = R1_out;
  assign R3_in = R2_out;
  assign R3_out = Done;
  assign Y0 = R1_out;
  assign Y1 = Done;
endmodule
